# Fritzing sketch SchematicSensorRobP1 (saved by Fritzing 0.9.4)
breadboards: 1

parts:
  Sensor_1 = RELAY [package=OJ]
  Sensor_2 = RELAY [package=OJ]
  Sensor_3 = RELAY [package=OJ]
  R1 = Resistor [tolerance=±5% resistance=220 package=THT]
  Arduino_Mega_2560 = Arduino Mega 2560 (Rev3)
  Part2 = Arduino Nano (Rev3.0)
  T1 = NPN-Transistor [package="SOT-23 [SMD]"]
  T2 = NPN-Transistor [package="SOT-23 [SMD]"]
  T3 = NPN-Transistor [package="SOT-23 [SMD]"]
  R2 = Resistor [tolerance=±5% resistance=220 package=THT]
  R3 = Resistor [tolerance=±5% resistance=220 package=THT]
  R4 = Resistor [tolerance=±5% resistance=220 package=THT]
  R5 = Resistor [tolerance=±5% resistance=220 package=THT]
  R6 = Resistor [tolerance=±5% resistance=220 package=THT]
  R7 = Resistor [tolerance=±5% resistance=220 package=THT]
  R8 = Resistor [tolerance=±5% resistance=220 package=THT]
  R9 = Resistor [tolerance=±5% resistance=220 package=THT]
  R10 = Resistor [tolerance=±5% resistance=220 package=THT]
  DC12V = DC Power [voltage=12V]

nets:
  GND: Sensor_1.COIL2, Sensor_2.COIL2, Sensor_3.COIL2, Arduino_Mega_2560.GND, Part2.GND, R8.Pin_0, R9.Pin_0, R10.Pin_0, DC12V.V-
  N1: Sensor_1.MAIN, R2.Pin_0
  N2: Sensor_1.NO, Sensor_1.COIL1, T1.2, R5.Pin_0
  N3: Sensor_2.MAIN, R3.Pin_0
  N4: Sensor_2.NO, Sensor_2.COIL1, T2.2, R6.Pin_0
  N5: Sensor_3.MAIN, R4.Pin_0
  N6: Sensor_3.NO, Sensor_3.COIL1, T3.2, R7.Pin_0
  VIN: R1.Pin_0, Arduino_Mega_2560.VIN, Part2.VIN, DC12V.V+
  N7: R1.Pin_1, T1.0, T2.0, T3.0
  N8: Arduino_Mega_2560.D38, T1.1
  N9: Arduino_Mega_2560.D39, R2.Pin_1
  N10: Arduino_Mega_2560.D40, T2.1
  N11: Arduino_Mega_2560.D41, R3.Pin_1
  N12: Arduino_Mega_2560.D42, T3.1
  N13: Arduino_Mega_2560.D43, R4.Pin_1
  N14: Arduino_Mega_2560.D44, Part2.D11/MOSI
  N15: Arduino_Mega_2560.D45, Part2.D10
  N16: Arduino_Mega_2560.D46, Part2.D9
  N17: Arduino_Mega_2560.D47, Part2.D8
  N18: Part2.D2, R5.Pin_1
  N19: Part2.D3, R6.Pin_1
  N20: Part2.D4, R7.Pin_1
  N21: Part2.D5, R8.Pin_1
  N22: Part2.D6, R9.Pin_1
  N23: Part2.D7, R10.Pin_1
